# Fritzing sketch analog multiplexer half (saved by Fritzing 0.9.2b)
breadboards: 1

parts:
  R1 = Rotary Potentiometer (Small) [maximum_resistance=100kΩ package=THT]
  R2 = Rotary Potentiometer (Small) [maximum_resistance=100kΩ package=THT]
  IC1 = IC, DIP package, 16 pins [chip_label=CD74HC4051E]
  Part1 = Arduino Uno (Rev3)

nets:
  N1: R1.leg1, R2.leg1, IC1.pin6, IC1.pin8, Part1.GND
  N2: R1.wiper, IC1.pin14, Part1.A2
  N3: R1.leg2, R2.leg2, IC1.pin16, Part1.5V
  N4: R2.wiper, IC1.pin13, Part1.A1
  N5: IC1.pin3, Part1.A0
  N6: IC1.pin9, Part1.D4
  N7: IC1.pin10, Part1.D5_PWM
  N8: IC1.pin11, Part1.D6_PWM
